# Fritzing sketch schema (saved by Fritzing 0.9.3b)

parts:
  a_un_composant_avec_l'id_fritzing = Arduino Uno (Rev3)
  Grove1 = Grove Buzz
  kEYPAD_MATRICIAL_1 = KEYPAD 4x3
  LCM1602_IIC1 = LCM1602 IIC [part_number="LCM1602 IIC" chip_label="LCM1602 IIC" package="DIP (Dual Inline) [THT]"]
  LCD1 = LCD screen

nets:
  N1: a_un_composant_avec_l'id_fritzing.A4/SDA, LCM1602_IIC1.SDA
  N2: a_un_composant_avec_l'id_fritzing.A5/SCL, LCM1602_IIC1.SCL
  N3: a_un_composant_avec_l'id_fritzing.D8, kEYPAD_MATRICIAL_1.arrow2
  N4: a_un_composant_avec_l'id_fritzing.D9_PWM, kEYPAD_MATRICIAL_1.col2
  N5: a_un_composant_avec_l'id_fritzing.D10_PWM/SS, kEYPAD_MATRICIAL_1.arrow1
  N6: a_un_composant_avec_l'id_fritzing.D11_PWM/MOSI, kEYPAD_MATRICIAL_1.col1
  N7: a_un_composant_avec_l'id_fritzing.D12/MISO, Grove1.SIG
  GND: a_un_composant_avec_l'id_fritzing.GND, Grove1.GND, LCM1602_IIC1.GND
  N8: a_un_composant_avec_l'id_fritzing.D5_PWM, kEYPAD_MATRICIAL_1.arrow4
  N9: a_un_composant_avec_l'id_fritzing.D6_PWM, kEYPAD_MATRICIAL_1.arrow3
  N10: a_un_composant_avec_l'id_fritzing.D7, kEYPAD_MATRICIAL_1.col3
  3V3: a_un_composant_avec_l'id_fritzing.3V3, Grove1.VCC
  5V: a_un_composant_avec_l'id_fritzing.5V, LCM1602_IIC1.VCC
  VSS: LCM1602_IIC1.VSS, LCD1.VSS
  VDD: LCM1602_IIC1.VDD, LCD1.VDD
  N11: LCM1602_IIC1.V0, LCD1.V0
  N12: LCM1602_IIC1.RS, LCD1.RS
  N13: LCM1602_IIC1.RW, LCD1.R/W
  N14: LCM1602_IIC1.E, LCD1.E
  N15: LCM1602_IIC1.D0, LCD1.DB0
  N16: LCM1602_IIC1.D1, LCD1.DB1
  N17: LCM1602_IIC1.D2, LCD1.DB2
  N18: LCM1602_IIC1.D3, LCD1.DB3
  N19: LCM1602_IIC1.D4, LCD1.DB4
  N20: LCM1602_IIC1.D5, LCD1.DB5
  N21: LCM1602_IIC1.D6, LCD1.DB6
  N22: LCM1602_IIC1.D7, LCD1.DB7
  N23: LCM1602_IIC1.A, LCD1.LED+
  N24: LCM1602_IIC1.K, LCD1.LED-

custom parts:
  KEYPAD 4x3: KEYPAD matricial de 12 botones, 4 filas x 3 columnas
  LCM1602 IIC: I2C-Module to use a 1602 or 2004 LCD on with the wire.h libory Serial LCD Modul
