# Fritzing sketch Platine (saved by Fritzing 0.9.3b)
breadboards: 1

parts:
  Matrix_keypad1 = KEYPAD 4x4
  LCD1 = LCD screen
  J1 = Piezo Speaker  # not connected
  Composant1 = Arduino Uno (Rev3)

nets:
  N1: Matrix_keypad1.row4, Composant1.D5_PWM
  VSS: LCD1.VSS, LCD1.VDD, LCD1.R/W, LCD1.LED+
  N2: LCD1.RS, Composant1.D2
  N3: LCD1.DB4, Composant1.A4/SDA
  N4: LCD1.DB5, Composant1.A3
  N5: LCD1.DB6, Composant1.A2
  N6: LCD1.DB7, Composant1.A1

custom parts:
  KEYPAD 4x4: Matrix keypad 16 buttons, 4 rows x 4 columns
