# Fritzing sketch ShémaCablageRaspberry (saved by Fritzing 0.9.3b)
breadboards: 1

parts:
  Raspberry_Pi_1 = Raspberry Pi 3 [part_number=RPI-3-V1.2]
  U1 = RFID RC522 SIP - 8 pins [chip_label="RFID RC522" package="SIP (Single Inline) [THT]"]
  U2 = RFID RC522 SIP - 8 pins [chip_label="RFID RC522" package="SIP (Single Inline) [THT]"]
  U3 = RFID RC522 SIP - 8 pins [chip_label="RFID RC522" package="SIP (Single Inline) [THT]"]
  U4 = RFID RC522 SIP - 8 pins [chip_label="RFID RC522" package="SIP (Single Inline) [THT]"]
  LED1 = LED - 5mm [color="Red (633nm)" package="5 mm [THT]"]
  R1 = Resistor [tolerance=±10% resistance=150 package=THT]
  LED2 = LED - 5mm [color="Red (633nm)" package="5 mm [THT]"]
  LED3 = LED - 5mm [color="Red (633nm)" package="5 mm [THT]"]
  LED4 = LED - 5mm [color="Red (633nm)" package="5 mm [THT]"]
  KY-1 = Keyes Relay [package=THT]
  R2 = Resistor [tolerance=±5% resistance=150 package=THT]
  R3 = Resistor [tolerance=±5% resistance=150 package=THT]
  R4 = Resistor [tolerance=±5% resistance=150 package=THT]

nets:
  VCC: Raspberry_Pi_1.3v3, U1.VCC, U2.VCC, U3.VCC, U4.VCC
  N1: Raspberry_Pi_1.GPIO2, U1.RST, U2.RST, U3.RST, U4.RST
  N2: Raspberry_Pi_1.GPIO3, LED1.anode
  N3: Raspberry_Pi_1.GPIO4, LED2.anode
  GND: Raspberry_Pi_1.GND, U1.GND, U2.GND, U3.GND, U4.GND, R1.Pin_0, KY-1.ground, R2.Pin_0, R3.Pin_0, R4.Pin_0
  N4: Raspberry_Pi_1.GPIO17, LED3.anode
  N5: Raspberry_Pi_1.GPIO27, LED4.anode
  N6: Raspberry_Pi_1.GPIO10, U1.MOSI, U2.MOSI, U3.MOSI, U4.MOSI
  N7: Raspberry_Pi_1.GPIO9, U1.MISO, U2.MISO, U3.MISO, U4.MISO
  N8: Raspberry_Pi_1.GPIO11, U1.SCK, U2.SCK, U3.SCK, U4.SCK
  N9: Raspberry_Pi_1.GPIO21, KY-1.signal
  N10: Raspberry_Pi_1.GPIO20, U4.NSS
  N11: Raspberry_Pi_1.GPIO16, U3.NSS
  N12: Raspberry_Pi_1.GPIO7, U2.NSS
  N13: Raspberry_Pi_1.GPIO8, U1.NSS
  N14: Raspberry_Pi_1.GPIO24, U1.IRQ, U2.IRQ, U3.IRQ, U4.IRQ
  N15: Raspberry_Pi_1.5V, KY-1.power
  N16: LED1.cathode, R1.Pin_1
  N17: LED2.cathode, R4.Pin_1
  N18: LED3.cathode, R3.Pin_1
  N19: LED4.cathode, R2.Pin_1

notes:
  12V VDC
  Gâche électrique

custom parts:
  RFID RC522 SIP - 8 pins: A SIP stand-in part for RFID RC522 . With 8 pins on a 300 mil single inline package (SIP) footprint.
  Keyes Relay: The Keyes 5V relay module is suitable for SCM development, home appliance control. It uses a 5V~12V TIL control signal which can control DC / AC signal.
